// Logisim project ULA+Teclado.circ as structural Verilog: 1 circuit, main circuit main
module main (
  input  in_1,
  input  in_2,
  input  in_3,
  input  A,
  input  B,
  input  in_6,
  input  [6:0] in_7,
  input  [2:0] in_8,
  input  in_9,
  input  [6:0] in_10,
  output out_11,
  output [6:0] out_12,
  output out_13
);

  wire adder_1_out, and_3_out, clock_1_out, clock_2_out, divider_1_out, multiplier_1_out, not_1_out,
       not_2_out, or_1_out, subtractor_1_out;

  Keyboard keyboard_1 (.clk(clock_1_out), .re(in_1), .clr(in_2), .avail(out_11), .data(out_12));
  Clock clock_1 (.out(clock_1_out));
  Clock clock_2 (.out(clock_2_out));
  TTY tty_1 (.data(out_12), .clk(clock_2_out), .we(in_3), .clr(in_6));
  // AND_Gate and_1 has open pins: in0=out_12, in1=in_7, out=open
  // AND_Gate and_2 has open pins: in0=out_12, in1=in_10, out=open
  not not_1 (not_1_out, B);
  not not_2 (not_2_out, A);
  Adder #(.width(1)) adder_1 (.a(B), .b(A), .out(adder_1_out));  // open: cin, cout
  Subtractor #(.width(1)) subtractor_1 (.a(B), .b(A), .out(subtractor_1_out));  // open: bin, bout
  Multiplier #(.width(1)) multiplier_1 (.a(B), .b(A), .out(multiplier_1_out));  // open: cin, cout
  Divider #(.width(1)) divider_1 (.a(B), .b(A), .out(divider_1_out));  // open: upper, rem
  and and_3 (and_3_out, B, A);
  or or_1 (or_1_out, B, A);
  Multiplexer #(.select(3)) multiplexer_1 (
    .in0(and_3_out), .in1(or_1_out), .in2(not_1_out), .in3(not_2_out), .in4(adder_1_out),
    .in5(subtractor_1_out), .in6(multiplier_1_out), .in7(divider_1_out), .out(out_13), .sel(in_8), .en(in_9));
endmodule
